# Fritzing sketch train_lantern (saved by Fritzing 0.9.3b)

parts:
  LED1 = prefix0000
  LED2 = prefix0000
  LED3 = prefix0000
  LED4 = prefix0000
  U2 = POT_SWITCH [package=pot_pth]
  S1 = Round Pushbutton
  LED5 = smd LED [color="Red (633nm)" package="0805 [SMD]"]
  Part1 = Adafruit Trinket M0 [part_number="Adafruit #3500"]
  VCC1 = 4 x AAA Battery Mount

nets:
  N1: LED1.connector1, LED2.connector1, LED3.connector1, LED4.connector1, Part1.3.3V
  N2: LED1.connector2, Part1.D4_A2_PA06_TXD_MOSI
  N3: LED1.connector3, LED2.connector3, LED3.connector3, LED4.connector3, Part1.GND
  N4: LED1.connector4, LED2.connector2
  N5: LED2.connector4, LED3.connector2
  N6: LED3.connector4, LED4.connector2
  N7: U2.G$2_1, Part1.D3_A3_PA07_RXD_SCK
  N8: U2.G$1_E, S1.leg1, LED5.cathode, VCC1.-
  N9: U2.G$2_2, Part1.VBAT
  N10: U2.G$1_S, VCC1.+
  N11: S1.leg0, Part1.D2_A1_PA09_SCL_MISO
  N12: LED5.anode, Part1.D1_A0_PA02
